# Fritzing sketch connor-disco-light-long (saved by Fritzing 0.7.11b)
breadboards: 3

parts:
  U1 = atmega328 [package=dip]
  C4 = Ceramic Capacitor [capacitance=100nF package="200 mil [THT, multilayer]"]
  C5 = Ceramic Capacitor [capacitance=22µF package="200 mil [THT, multilayer]"]
  C6 = Ceramic Capacitor [capacitance=22µF package="200 mil [THT, multilayer]"]
  R1 = 10k Ω Resistor [package=THT]
  XTAL1 = Crystal [frequency="16 Mhz" package=THT]
  J1 = double row male pin header, 2 pins [form="♂ (male)"]
  J3 = double row male pin header, 2 pins [form="♂ (male)"]
  J4 = Piezo Speaker
  J5 = Basic Servo
  J6 = Basic Servo
  S1 = Toggle Switch [package=THT]  # not connected
  R2 = 1M Ω Resistor [package=THT]
  U6 = 74HC595 [package="DIP16 [THT]"]
  U7 = 74HC595 [package="DIP16 [THT]"]
  U8 = 74HC595 [package="DIP16 [THT]"]
  J8 = male pin header, 12 pins [form="♂ (male)"]
  R3 = 1M Ω Resistor [package=THT]
  R4 = 1M Ω Resistor [package=THT]
  R5 = 1M Ω Resistor [package=THT]
  R6 = 1M Ω Resistor [package=THT]
  R7 = 1M Ω Resistor [package=THT]
  R8 = 1M Ω Resistor [package=THT]
  R9 = 1M Ω Resistor [package=THT]
  R10 = 1M Ω Resistor [package=THT]
  R11 = 1M Ω Resistor [package=THT]
  R12 = 1M Ω Resistor [package=THT]
  R13 = 1M Ω Resistor [package=THT]
  R14 = 1M Ω Resistor [package=THT]
  R15 = 1M Ω Resistor [package=THT]
  R16 = 1M Ω Resistor [package=THT]
  R17 = 1M Ω Resistor [package=THT]
  J9 = male pin header, 12 pins [form="♂ (male)"]

nets:
  N1: U1.RESET, U1.D0_(RX), C4.1, R1.Pin_0, J3.pin2
  N2: U1.D1_(TX), J3.pin1
  VCC: U1.D4, U1.VCC, U1.AVCC, R1.Pin_1, J1.pin1, J5.vcc, J6.vcc
  GND: U1.GND, C5.0, C6.0, J4.pin1, J5.gnd, J6.gnd
  N3: U1.XLAT1, C6.1, XTAL1.pin_1
  N4: U1.XLAT2, C5.1, XTAL1.pin_0
  N5: U1.D5_(PWM), J6.pulse
  N6: U1.D6_(PWM), J5.pulse
  N7: U1.D11_(PWM), U7.DS
  N8: U1.D13, U6.DS
  N9: R2.Pin_0, J8.pin2
  N10: R2.Pin_1, U6.Q7
  N11: U6.Q1, R8.Pin_1
  N12: U6.Q2, R7.Pin_1
  N13: U6.Q3, R6.Pin_1
  N14: U6.Q4, R5.Pin_1
  N15: U6.Q5, R4.Pin_1
  N16: U6.Q6, R3.Pin_1
  N17: U6.Q0, R9.Pin_1
  N18: U7.Q1, R12.Pin_1
  N19: U7.Q2, R16.Pin_1
  N20: U7.Q3, R17.Pin_1
  N21: U7.Q4, R14.Pin_1
  N22: U7.Q5, R13.Pin_1
  N23: U7.Q6, R11.Pin_1
  N24: U7.Q7, R10.Pin_1
  N25: U7.Q0, R15.Pin_1
  N26: U8.Q1, J9.pin7
  N27: U8.Q2, J9.pin4
  N28: U8.Q3, J9.pin1
  N29: U8.Q4, J8.pin10
  N30: U8.Q5, J8.pin7
  N31: U8.Q6, J8.pin4
  N32: U8.Q7, J8.pin1
  N33: J8.pin3, R10.Pin_0
  N34: J8.pin5, R3.Pin_0
  N35: J8.pin6, R11.Pin_0
  N36: J8.pin8, R4.Pin_0
  N37: J8.pin9, R13.Pin_0
  N38: J8.pin11, R5.Pin_0
  N39: J8.pin12, R14.Pin_0
  N40: R6.Pin_0, J9.pin2
  N41: R7.Pin_0, J9.pin5
  N42: R8.Pin_0, J9.pin8
  N43: R9.Pin_0, J9.pin11
  N44: R12.Pin_0, J9.pin9
  N45: R15.Pin_0, J9.pin12
  N46: R16.Pin_0, J9.pin6
  N47: R17.Pin_0, J9.pin3
